# Fritzing sketch home_climate (saved by Fritzing 0.9.2b)
circuit board: 8.46667cm x 5.64444cm
breadboards: 1

parts:
  LCD1 = LCD screen
  U1 = 74HC595 [package="DIP16 [THT]"]
  Часть1 = Arduino Uno (Rev3)
  R1 = Rotary Potentiometer (Small) [maximum_resistance=100kΩ package=THT]
  R2 = Resistor [tolerance=±5% resistance=220 package=THT]

nets:
  GND: LCD1.VSS, LCD1.R/W, U1.GND, U1.OE, Часть1.GND, R1.leg2, R2.Pin_1
  VDD: LCD1.VDD, LCD1.LED+, U1.Q7', U1.VCC, Часть1.5V, R1.leg1
  N1: LCD1.V0, R1.wiper
  N2: LCD1.RS, U1.Q1
  N3: LCD1.E, LCD1.DB0, LCD1.DB1, LCD1.DB2, LCD1.DB3, U1.Q3
  N4: LCD1.DB4, U1.Q4
  N5: LCD1.DB5, U1.Q5
  N6: LCD1.DB6, U1.Q6
  N7: LCD1.DB7, U1.Q7
  N8: LCD1.LED-, R2.Pin_0
  N9: U1.SH_CP, Часть1.D13/SCK
  N10: U1.ST_CP, Часть1.D10_PWM/SS
  N11: U1.DS, Часть1.D11_PWM/MOSI
